// Digital circuit DISK-CS-GAL.dig as structural Verilog
module DISK_CS_GAL (
  input  nCSxDISK,
  input  bA3,
  input  bA2,
  output nCSxFDC,
  output nCSxPPIDE,
  output nCSxSPIxLED,
  output nCSxPPIDExLED,
  output nCSxSPI
);

  wire not_1_out, not_2_out, or_2_out;

  not not_1 (not_1_out, bA3);
  or or_1 (nCSxFDC, nCSxDISK, bA3);
  or or_2 (or_2_out, nCSxDISK, not_1_out);
  not not_2 (not_2_out, bA2);
  or or_3 (nCSxPPIDE, or_2_out, bA2);
  or or_4 (nCSxSPI, or_2_out, not_2_out);
  or or_5 (nCSxSPIxLED, nCSxSPI, nCSxSPI);
  or or_6 (nCSxPPIDExLED, nCSxPPIDE, nCSxPPIDE);

  // Notes on the sheet:
  //   nCSxDISK: pin 2
  //   bA3: pin 3
  //   nCSxFDC: pin 19
  //   nCSxPPIDE: pin 18
  //   bA2: pin 4
  //   nCSxSPIxLED: pin 16
  //   nCSxPPIDExLED: pin 15
  //   nCSxSPI: pin 17
  //   DISK CS GAL16V8
endmodule
