// Digital circuit Z80-processor-DMA.dig as structural Verilog
module Z80_processor_DMA (
  input  nDREQ0,
  input  nDREQ1,
  input  nCPUxWR,
  input  nCPUxRESET,
  input  CPU_D0,
  input  CPU_D1,
  input  CPU_D2,
  input  CPU_D3,
  input  nCPUxIORQ,
  input  nCPUxM1,
  input  CPUxA2,
  input  Q2,
  input  Q3,
  input  CPUxA4,
  input  CPUxA5,
  input  CPUxA6,
  input  CPUxA7,
  input  Q4,
  input  Q5,
  input  Q6,
  input  Q7,
  input  R4,
  input  R5,
  input  R6,
  input  R7,
  input  CPUxA0,
  input  CPUxA1,
  input  nCPUxWAIT,
  input  nCPUxBUSACK,
  input  nDMAxINTxPULSE1,
  input  nDMAxINTxPULSE2,
  input  CPUxA3,
  input  nDMAxBAO2,
  output DMAxRDY1,
  output DMAxRDY2,
  output nDMAxRESET1,
  output nDMAxRESET2,
  output nFPxLATCH,
  output nDMAxCS1,
  output nDMAxCS2,
  output nBUSxEN,
  output DATAxXFER,
  output IOxSEL,
  output nCSxMAP,
  output nCSxUART
);

  wire _74139_1_p4, _74139_1_p9, _74139_1_p10, _74139_1_p12, _74157_1_p9, _74175_1_p9, _74175_1_p10,
       _74175_1_p11, _74175_1_p12, _74688_2_p20, and_1_out, not_2_out, not_3_out, not_4_out, or_7_out;

  not not_1 (nBUSxEN, nDMAxBAO2);
  not not_2 (not_2_out, CPUxA3);
  // _74139 _74139_1: pin names not known; wires that end beside it: 1'b1, 1'b1, 1'b1, _74139_1_p4, CPUxA0, CPUxA1, 1'b1, 1'b0, _74139_1_p9, _74139_1_p10, nFPxLATCH, _74139_1_p12
  // _74157 _74157_1: pin names not known; wires that end beside it: nCPUxWAIT, nCPUxWAIT, 1'b0, 1'b0, _74139_1_p9, _74139_1_p10, 1'b0, 1'b0, _74157_1_p9, 1'b0, 1'b1, 1'b0, nDMAxCS1, nDMAxCS2
  or or_1 (_74157_1_p9, nBUSxEN, nCPUxBUSACK);
  and and_1 (and_1_out, nDMAxINTxPULSE1, nDMAxINTxPULSE2);
  nand nand_1 (IOxSEL, _74139_1_p4, _74688_2_p20);
  or or_2 (nCSxMAP, _74688_2_p20, CPUxA3);
  or or_3 (nCSxUART, _74688_2_p20, not_2_out);
  // _74688 _74688_1: pin names not known; wires that end beside it: nCPUxIORQ, nCPUxM1, 1'b1, 1'b1, 1'b1, CPUxA2, Q2, CPUxA3, Q3, CPUxA4, Q4, CPUxA5, Q5, CPUxA6, Q6, CPUxA7, Q7, 1'b1, 1'b0, _74139_1_p4
  or or_4 (DATAxXFER, _74157_1_p9, and_1_out);
  not not_3 (not_3_out, nDREQ0);
  not not_4 (not_4_out, nDREQ1);
  // _74688 _74688_2: pin names not known; wires that end beside it: nCPUxIORQ, nCPUxM1, 1'b1, 1'b1, 1'b1, 1'b1, 1'b1, 1'b1, 1'b1, CPUxA4, R4, CPUxA5, R5, CPUxA6, R6, CPUxA7, R7, 1'b1, 1'b0, _74688_2_p20
  or or_5 (DMAxRDY1, not_3_out, _74175_1_p9);
  or or_6 (DMAxRDY2, not_4_out, _74175_1_p10);
  or or_7 (or_7_out, nCPUxWR, _74139_1_p12);
  // _74175 _74175_1: pin names not known; wires that end beside it: CPU_D0, CPU_D1, CPU_D2, CPU_D3, or_7_out, nCPUxRESET, 1'b1, 1'b0, _74175_1_p9, _74175_1_p10, _74175_1_p11, _74175_1_p12
  and and_2 (nDMAxRESET1, _74175_1_p11, nCPUxRESET);
  and and_3 (nDMAxRESET2, nCPUxRESET, _74175_1_p12);

  // Notes on the sheet:
  //   DMA CS V4 GAL22V10
  //   ~LOCALxDMA
  //   ~DMAxADDR
  //   Assert ~BUSxEN unless an
  //   external bus master is active.
  //   DMA RDY
  //   ~CSxIO
  //   RDY1
  //   ~USRxRESET1
  //   ~USRxRESET2
  //   ~DMAxRDYxWR
  //   RDY2
endmodule
